// Logisim project CPU_PROJ.circ as structural Verilog: 2 circuits, main circuit main
module main (
  input  _4,
  input  in_2,
  input  _2,
  input  in_4,
  input  in_5,
  input  _1,
  input  in_7
);

  ALU_4BIT alu_4bit_1 (
    .in_1(_4), .in_2(in_2), .in_3(_2), .in_4(in_4), .in_5(in_5), .in_6(_1), .in_7(in_7));  // open: out_8, out_9, out_10, out_11
endmodule

module ALU_4BIT (
  input  in_1,
  input  in_2,
  input  in_3,
  input  in_4,
  input  in_5,
  input  in_6,
  input  in_7,
  output out_8,
  output out_9,
  output out_10,
  output out_11
);

  wire and_1_out, and_2_out, and_3_out, and_4_out, or_1_out, or_2_out, or_3_out, or_4_out, xor_1_out,
       xor_2_out, xor_3_out, xor_4_out;

  xor xor_1 (xor_1_out, 1'b0, xor_2_out, 1'b0, and_1_out, or_1_out);
  and and_1 (and_1_out, 1'b0, xor_2_out, 1'b0, or_1_out);
  or or_1 (or_1_out, 1'b0, xor_2_out, 1'b0);
  xor xor_2 (xor_2_out, in_1, xor_3_out, in_2, and_2_out, or_2_out);
  and and_2 (and_2_out, in_1, xor_3_out, in_2, or_2_out);
  or or_2 (or_2_out, in_1, xor_3_out, in_2);
  xor xor_3 (xor_3_out, in_3, xor_4_out, in_4, and_3_out, or_3_out);
  and and_3 (and_3_out, in_3, xor_4_out, in_4, or_3_out);
  or or_3 (or_3_out, in_3, xor_4_out, in_4);
  xor xor_4 (xor_4_out, in_5, in_6, in_7, and_4_out, or_4_out);
  and and_4 (and_4_out, in_5, in_6, in_7, or_4_out);
  or or_4 (or_4_out, in_5, in_6, in_7);
  xor xor_5 (out_8, xor_1_out, and_1_out, or_1_out);
  xor xor_6 (out_9, xor_2_out, and_2_out, or_2_out);
  xor xor_7 (out_10, xor_3_out, and_3_out, or_3_out);
  xor xor_8 (out_11, xor_4_out, and_4_out, or_4_out);
endmodule
